// Logisim project 16.circ as structural Verilog: 8 circuits, main circuit main
module main (
  input  [3:0] in_1
);

  wire a_1_a, b_1_out_2, c_1_out_2, d_1_out_2, e_1_out_2, f_1_out_2, g_1_out_2;

  b b_1 (.in_1(in_1), .out_2(b_1_out_2));
  a a_1 (.a(a_1_a), .in_1(in_1));
  f f_1 (.in_1(in_1), .out_2(f_1_out_2));
  g g_1 (.in_1(in_1), .out_2(g_1_out_2));
  e e_1 (.in_1(in_1), .out_2(e_1_out_2));
  d d_1 (.in_1(in_1), .out_2(d_1_out_2));
  c c_1 (.in_1(in_1), .out_2(c_1_out_2));
  _7_Segment_Display u_7_segment_display_1 (
    .g(g_1_out_2), .f(f_1_out_2), .a(a_1_a), .b(b_1_out_2), .e(e_1_out_2), .d(d_1_out_2), .c(c_1_out_2));  // open: dp
endmodule

module a (
  input  [3:0] in_1,
  output a
);

  wire xnor_1_out;

  xnor xnor_1 (xnor_1_out, in_1[1], in_1[3]);
  or or_1 (a, xnor_1_out, in_1[0], in_1[2]);
endmodule

module b (
  input  [3:0] in_1,
  output out_2
);

  wire not_1_out, xnor_1_out;

  xnor xnor_1 (xnor_1_out, in_1[2], in_1[3]);
  not not_1 (not_1_out, in_1[1]);
  or or_1 (out_2, xnor_1_out, not_1_out);
endmodule

module c (
  input  [3:0] in_1,
  output out_2
);

  wire not_1_out;

  not not_1 (not_1_out, in_1[2]);
  or or_1 (out_2, in_1[1], not_1_out, in_1[3]);
endmodule

module d (
  input  [3:0] in_1,
  output out_2
);

  wire and_1_out, and_2_out, and_3_out, and_4_out;

  and and_1 (and_1_out, ~in_1[1], ~in_1[3]);  // AND_Gate
  and and_2 (and_2_out, ~in_1[1], in_1[2]);  // AND_Gate
  and and_3 (and_3_out, in_1[2], ~in_1[3]);  // AND_Gate
  and and_4 (and_4_out, in_1[1], ~in_1[2], in_1[3]);  // AND_Gate
  or or_1 (out_2, and_1_out, and_2_out, and_3_out, and_4_out, in_1[0]);
endmodule

module e (
  input  [3:0] in_1,
  output out_2
);

  wire and_1_out, and_2_out;

  and and_1 (and_1_out, ~in_1[1], ~in_1[3]);  // AND_Gate
  and and_2 (and_2_out, in_1[2], ~in_1[3]);  // AND_Gate
  or or_1 (out_2, and_1_out, and_2_out);
endmodule

module f (
  input  [3:0] in_1,
  output out_2
);

  wire and_1_out, and_2_out, and_3_out;

  and and_1 (and_1_out, ~in_1[2], ~in_1[3]);  // AND_Gate
  and and_2 (and_2_out, in_1[1], ~in_1[2]);  // AND_Gate
  and and_3 (and_3_out, in_1[1], ~in_1[3]);  // AND_Gate
  or or_1 (out_2, in_1[0], and_1_out, and_2_out, and_3_out);
endmodule

module g (
  input  [3:0] in_1,
  output out_2
);

  wire and_1_out, xor_1_out;

  xor xor_1 (xor_1_out, in_1[1], in_1[2]);
  and and_1 (and_1_out, in_1[2], ~in_1[3]);  // AND_Gate
  or or_1 (out_2, in_1[0], xor_1_out, and_1_out);
endmodule
